// Logisim project LAB11My.circ as structural Verilog: 2 circuits, main circuit ALU
module Shifter (
  input  [31:0] A,
  input  [4:0] shift,
  input  [1:0] selc,
  output [31:0] out_4
);

  wire [31:0] shifter_1_out, shifter_2_out, shifter_3_out;

  Shifter_part #(.width(32)) shifter_1 (.in(A), .\dist (shift), .out(shifter_1_out));
  Shifter_part #(.shift("lr"), .width(32)) shifter_2 (.in(A), .\dist (shift), .out(shifter_2_out));
  Shifter_part #(.shift("lr"), .width(32)) shifter_3 (.in(A), .\dist (shift), .out(shifter_3_out));
  Multiplexer #(.enable("true"), .select(2), .width(32)) multiplexer_1 (
    .in0(A), .in1(shifter_1_out), .in2(shifter_2_out), .in3(shifter_3_out), .out(out_4), .sel(selc));  // open: en
endmodule

module ALU (
  input  [1:0] shift_op,
  input  [31:0] A,
  input  [31:0] B,
  input  arith_op,
  input  [1:0] Alu_select,
  input  [1:0] logical_op,
  input  in_7,
  output [31:0] Output,
  output Zero,
  output Overflow
);

  wire xor_3_out;
  wire [31:0] adder_1_out, and_1_out, bit_extender_1_out, bit_extender_2_out, bit_extender_3_out,
       multiplexer_1_out, not_1_out, or_1_out, shifter_1_out_4, xor_1_out, xor_2_out;

  assign bit_extender_1_out = {{31{arith_op}}, arith_op};  // Bit_Extender bit_extender_1
  assign xor_1_out = B ^ bit_extender_1_out;  // XOR_Gate xor_1, 32 bits wide
  assign and_1_out = A & B;  // AND_Gate and_1, 32 bits wide
  assign or_1_out = A | B;  // OR_Gate or_1, 32 bits wide
  assign xor_2_out = A ^ B;  // XOR_Gate xor_2, 32 bits wide
  Shifter shifter_1 (.A(B), .shift(A[4:0]), .selc(shift_op), .out_4(shifter_1_out_4));
  Adder #(.width(32)) adder_1 (.a(A), .b(xor_1_out), .out(adder_1_out), .cin(arith_op), .cout(Overflow));
  assign not_1_out = ~or_1_out;  // NOT_Gate not_1, 32 bits wide
  Multiplexer #(.select(2), .width(32)) multiplexer_1 (
    .in0(and_1_out), .in1(or_1_out), .in2(not_1_out), .in3(xor_2_out), .out(multiplexer_1_out),
    .sel(logical_op));
  xor xor_3 (xor_3_out, Overflow, adder_1_out[31]);
  Multiplexer #(.select(2), .width(32)) multiplexer_2 (
    .in0(shifter_1_out_4), .in2(bit_extender_2_out), .in3(adder_1_out), .out(Output), .sel(Alu_select));  // open: in1
  assign bit_extender_2_out = {{31{xor_3_out}}, xor_3_out};  // Bit_Extender bit_extender_2
  assign bit_extender_3_out = {{31{in_7}}, in_7};  // Bit_Extender bit_extender_3
  Comparator #(.width(32)) comparator_1 (.a(Output), .b(bit_extender_3_out), .eq(Zero));  // open: gt, lt

  // Notes on the sheet:
  //   2240005893 MA01
  //   MOHAMMED NASSER ALMARHOON
endmodule
