// Logisim project LAB9my.circ as structural Verilog: 3 circuits, main circuit main
module main (
  input  A,
  input  B,
  input  Cin,
  output S,
  output Cout
);

  wire and_1_out, and_2_out, xor_1_out;

  xor xor_1 (xor_1_out, A, B);
  xor xor_2 (S, xor_1_out, Cin);
  and and_1 (and_1_out, A, B);
  and and_2 (and_2_out, xor_1_out, Cin);
  or or_1 (Cout, and_1_out, and_2_out);

  // Notes on the sheet:
  //   MOHAMMED NASSER ALMARHOON 2240005893
endmodule

module RCA8 (
  input  [7:0] in_1,
  input  in_2,
  input  [7:0] in_3,
  output [7:0] out_4,
  output out_5
);

  wire main_1_cout, main_2_cout, main_3_cout, main_4_cout, main_5_cout, main_6_cout, main_7_cout;

  main main_1 (.Cin(in_2), .A(in_1[0]), .B(in_3[0]), .S(out_4[0]), .Cout(main_1_cout));
  main main_2 (.Cin(main_1_cout), .A(in_1[1]), .B(in_3[1]), .S(out_4[1]), .Cout(main_2_cout));
  main main_3 (.Cin(main_2_cout), .A(in_1[2]), .B(in_3[2]), .S(out_4[2]), .Cout(main_3_cout));
  main main_4 (.Cin(main_3_cout), .A(in_1[3]), .B(in_3[3]), .S(out_4[3]), .Cout(main_4_cout));
  main main_5 (.Cin(main_4_cout), .A(in_1[4]), .B(in_3[4]), .S(out_4[4]), .Cout(main_5_cout));
  main main_6 (.Cin(main_5_cout), .A(in_1[5]), .B(in_3[5]), .S(out_4[5]), .Cout(main_6_cout));
  main main_7 (.Cin(main_6_cout), .A(in_1[6]), .B(in_3[6]), .S(out_4[6]), .Cout(main_7_cout));
  main main_8 (.Cin(main_7_cout), .A(in_1[7]), .B(in_3[7]), .S(out_4[7]), .Cout(out_5));
endmodule

module RCA32 (
  input  [31:0] in_1,
  input  in_2,
  input  [31:0] in_3,
  output [31:0] out_4,
  output out_5
);

  wire rca8_1_out_5, rca8_2_p4, rca8_3_out_5;

  RCA8 rca8_1 (.in_1(in_1[7:0]), .in_2(in_2), .in_3(in_3[7:0]), .out_5(rca8_1_out_5), .out_4(out_4[7:0]));
  // RCA8 rca8_2: pin names not known; wires that end beside it: in_1[15:8], in_3[15:8], rca8_1_out_5, rca8_2_p4, out_4[15:8]
  RCA8 rca8_3 (.in_1(in_1[23:16]), .in_2(rca8_2_p4), .in_3(in_3[23:16]), .out_5(rca8_3_out_5), .out_4(out_4[23:16]));
  RCA8 rca8_4 (.in_1(in_1[31:24]), .in_2(rca8_3_out_5), .in_3(in_3[31:24]), .out_5(out_5), .out_4(out_4[31:24]));
endmodule
