// Logisim project Lab8My.circ as structural Verilog: 2 circuits, main circuit main
module main (
  input  Carry_in,
  input  Input1,
  input  Input2,
  output Sum,
  output Carry_out
);

  wire and_2_out, AND_out, xor_1_out;

  xor xor_1 (xor_1_out, Input1, Input2);
  and AND (AND_out, Carry_in, xor_1_out);
  and and_2 (and_2_out, Input2, Input1);
  xor XOR_2 (Sum, xor_1_out, Carry_in);
  or OR (Carry_out, AND_out, and_2_out);

  // Notes on the sheet:
  //   2240005893
  //   MOHAMMED NASSER ALMARHOON
endmodule

module sec (
  input  in_1,
  input  [7:0] B,
  input  [7:0] A,
  output [7:0] Sum,
  output out_5
);

  wire main_1_carry_out, main_2_carry_out, main_3_carry_out, main_4_carry_out, main_5_carry_out,
       main_6_carry_out, main_7_carry_out;

  main main_1 (.Input1(A[0]), .Input2(B[0]), .Carry_in(in_1), .Sum(Sum[0]), .Carry_out(main_1_carry_out));
  main main_2 (.Input1(A[1]), .Input2(B[1]), .Carry_in(main_1_carry_out), .Sum(Sum[1]), .Carry_out(main_2_carry_out));
  main main_3 (.Input1(A[2]), .Input2(B[2]), .Carry_in(main_2_carry_out), .Sum(Sum[2]), .Carry_out(main_3_carry_out));
  main main_4 (.Input1(A[3]), .Input2(B[3]), .Carry_in(main_3_carry_out), .Sum(Sum[3]), .Carry_out(main_4_carry_out));
  main main_5 (.Input1(A[4]), .Input2(B[4]), .Carry_in(main_4_carry_out), .Sum(Sum[4]), .Carry_out(main_5_carry_out));
  main main_6 (.Input1(A[5]), .Input2(B[5]), .Carry_in(main_5_carry_out), .Sum(Sum[5]), .Carry_out(main_6_carry_out));
  main main_7 (.Input1(A[6]), .Input2(B[6]), .Carry_in(main_6_carry_out), .Sum(Sum[6]), .Carry_out(main_7_carry_out));
  main main_8 (.Input1(A[7]), .Input2(B[7]), .Carry_in(main_7_carry_out), .Sum(Sum[7]), .Carry_out(out_5));
endmodule
