// Logisim project lab10.my.circ as structural Verilog: 1 circuit, main circuit main
module main (
  input  [4:0] in_1,
  input  [4:0] in_2,
  input  [4:0] in_3,
  input  in_4,
  input  in_5,
  input  in_6,
  input  [31:0] in_7,
  output [31:0] out_8,
  output [31:0] out_9
);

  wire and_1_out, and_2_out, and_3_out, and_4_out, and_5_out, and_6_out, and_7_out, and_8_out, and_9_out,
       and_10_out, and_11_out, and_12_out, and_13_out, and_14_out, and_15_out, and_16_out, and_17_out,
       and_18_out, and_19_out, and_20_out, and_21_out, and_22_out, and_23_out, and_24_out, and_25_out,
       and_26_out, and_27_out, and_28_out, and_29_out, and_30_out, and_31_out, clock_1_out, decoder_1_out1,
       decoder_1_out2, decoder_1_out3, decoder_1_out4, decoder_1_out5, decoder_1_out6, decoder_1_out7,
       decoder_1_out8, decoder_1_out9, decoder_1_out10, decoder_1_out11, decoder_1_out12, decoder_1_out13,
       decoder_1_out14, decoder_1_out15, decoder_1_out16, decoder_1_out17, decoder_1_out18, decoder_1_out19,
       decoder_1_out20, decoder_1_out21, decoder_1_out22, decoder_1_out23, decoder_1_out24, decoder_1_out25,
       decoder_1_out26, decoder_1_out27, decoder_1_out28, decoder_1_out29, decoder_1_out30, decoder_1_out31,
       decoder_2_out0, decoder_2_out1, decoder_2_out2, decoder_2_out3, decoder_2_out4, decoder_2_out5,
       decoder_2_out6, decoder_2_out7, decoder_2_out8, decoder_2_out9, decoder_2_out10, decoder_2_out11,
       decoder_2_out12, decoder_2_out13, decoder_2_out14, decoder_2_out15, decoder_2_out16, decoder_2_out17,
       decoder_2_out18, decoder_2_out19, decoder_2_out20, decoder_2_out21, decoder_2_out22, decoder_2_out23,
       decoder_2_out24, decoder_2_out25, decoder_2_out26, decoder_2_out27, decoder_2_out28, decoder_2_out29,
       decoder_2_out30, decoder_2_out31, decoder_3_out0, decoder_3_out1, decoder_3_out2, decoder_3_out3,
       decoder_3_out4, decoder_3_out5, decoder_3_out6, decoder_3_out7, decoder_3_out8, decoder_3_out9,
       decoder_3_out10, decoder_3_out11, decoder_3_out12, decoder_3_out13, decoder_3_out14, decoder_3_out15,
       decoder_3_out16, decoder_3_out17, decoder_3_out18, decoder_3_out19, decoder_3_out20, decoder_3_out21,
       decoder_3_out22, decoder_3_out23, decoder_3_out24, decoder_3_out25, decoder_3_out26, decoder_3_out27,
       decoder_3_out28, decoder_3_out29, decoder_3_out30, decoder_3_out31;
  wire [31:0] controlled_buffer_55_out, register_1_q, register_2_q, register_3_q, register_4_q, register_5_q,
       register_6_q, register_7_q, register_8_q, register_9_q, register_10_q, register_11_q, register_12_q,
       register_13_q, register_14_q, register_15_q, register_16_q, register_17_q, register_18_q,
       register_19_q, register_20_q, register_21_q, register_22_q, register_23_q, register_24_q,
       register_25_q, register_26_q, register_27_q, register_28_q, register_29_q, register_30_q,
       register_31_q;

  Decoder #(.select(5)) decoder_1 (
    .out1(decoder_1_out1), .out2(decoder_1_out2), .out3(decoder_1_out3), .out4(decoder_1_out4),
    .out5(decoder_1_out5), .out6(decoder_1_out6), .out7(decoder_1_out7), .out8(decoder_1_out8),
    .out9(decoder_1_out9), .out10(decoder_1_out10), .out11(decoder_1_out11), .out12(decoder_1_out12),
    .out13(decoder_1_out13), .out14(decoder_1_out14), .out15(decoder_1_out15), .out16(decoder_1_out16),
    .out17(decoder_1_out17), .out18(decoder_1_out18), .out19(decoder_1_out19), .out20(decoder_1_out20),
    .out21(decoder_1_out21), .out22(decoder_1_out22), .out23(decoder_1_out23), .out24(decoder_1_out24),
    .out25(decoder_1_out25), .out26(decoder_1_out26), .out27(decoder_1_out27), .out28(decoder_1_out28),
    .out29(decoder_1_out29), .out30(decoder_1_out30), .out31(decoder_1_out31), .sel(in_3), .en(in_4));  // open: out0
  and and_1 (and_1_out, decoder_1_out1, in_5);
  and and_2 (and_2_out, decoder_1_out2, in_5);
  and and_3 (and_3_out, decoder_1_out3, in_5);
  and and_4 (and_4_out, decoder_1_out4, in_5);
  and and_5 (and_5_out, decoder_1_out5, in_5);
  and and_6 (and_6_out, decoder_1_out6, in_5);
  and and_7 (and_7_out, decoder_1_out7, in_5);
  and and_8 (and_8_out, decoder_1_out8, in_5);
  and and_9 (and_9_out, decoder_1_out9, in_5);
  and and_10 (and_10_out, decoder_1_out10, in_5);
  and and_11 (and_11_out, decoder_1_out11, in_5);
  and and_12 (and_12_out, decoder_1_out12, in_5);
  and and_13 (and_13_out, decoder_1_out13, in_5);
  and and_14 (and_14_out, decoder_1_out14, in_5);
  and and_15 (and_15_out, decoder_1_out15, in_5);
  and and_16 (and_16_out, decoder_1_out16, in_5);
  and and_17 (and_17_out, decoder_1_out17, in_5);
  and and_18 (and_18_out, decoder_1_out18, in_5);
  and and_19 (and_19_out, decoder_1_out19, in_5);
  and and_20 (and_20_out, decoder_1_out20, in_5);
  and and_21 (and_21_out, decoder_1_out21, in_5);
  and and_22 (and_22_out, decoder_1_out22, in_5);
  and and_23 (and_23_out, decoder_1_out23, in_5);
  and and_24 (and_24_out, decoder_1_out24, in_5);
  and and_25 (and_25_out, decoder_1_out25, in_5);
  and and_26 (and_26_out, decoder_1_out26, in_5);
  and and_27 (and_27_out, decoder_1_out27, in_5);
  and and_28 (and_28_out, decoder_1_out28, in_5);
  and and_29 (and_29_out, decoder_1_out29, in_5);
  and and_30 (and_30_out, decoder_1_out30, in_5);
  and and_31 (and_31_out, decoder_1_out31, in_5);
  Clock clock_1 (.out(clock_1_out));
  Register #(.width(32)) register_1 (.D(in_7), .en(and_1_out), .Q(register_1_q), .clk(clock_1_out), .clr(in_6));
  assign out_8 = decoder_2_out1 ? register_1_q : 32'bz;  // Controlled_Buffer controlled_buffer_1
  Register #(.width(32)) register_2 (.D(in_7), .en(and_2_out), .Q(register_2_q), .clk(clock_1_out), .clr(in_6));
  assign out_8 = decoder_2_out2 ? register_2_q : 32'bz;  // Controlled_Buffer controlled_buffer_2
  Register #(.width(32)) register_3 (.D(in_7), .en(and_3_out), .Q(register_3_q), .clk(clock_1_out), .clr(in_6));
  assign out_8 = decoder_2_out3 ? register_3_q : 32'bz;  // Controlled_Buffer controlled_buffer_3
  Register #(.width(32)) register_4 (.D(in_7), .en(and_4_out), .Q(register_4_q), .clk(clock_1_out), .clr(in_6));
  assign out_8 = decoder_2_out4 ? register_4_q : 32'bz;  // Controlled_Buffer controlled_buffer_4
  Register #(.width(32)) register_5 (.D(in_7), .en(and_5_out), .Q(register_5_q), .clk(clock_1_out), .clr(in_6));
  assign out_8 = decoder_2_out5 ? register_5_q : 32'bz;  // Controlled_Buffer controlled_buffer_5
  Register #(.width(32)) register_6 (.D(in_7), .en(and_6_out), .Q(register_6_q), .clk(clock_1_out), .clr(in_6));
  assign out_8 = decoder_2_out6 ? register_6_q : 32'bz;  // Controlled_Buffer controlled_buffer_6
  Register #(.width(32)) register_7 (.D(in_7), .en(and_7_out), .Q(register_7_q), .clk(clock_1_out), .clr(in_6));
  assign out_8 = decoder_2_out7 ? register_7_q : 32'bz;  // Controlled_Buffer controlled_buffer_7
  Register #(.width(32)) register_8 (.D(in_7), .en(and_8_out), .Q(register_8_q), .clk(clock_1_out), .clr(in_6));
  assign out_8 = decoder_2_out8 ? register_8_q : 32'bz;  // Controlled_Buffer controlled_buffer_8
  Register #(.width(32)) register_9 (.D(in_7), .en(and_9_out), .Q(register_9_q), .clk(clock_1_out), .clr(in_6));
  assign out_8 = decoder_2_out9 ? register_9_q : 32'bz;  // Controlled_Buffer controlled_buffer_9
  Register #(.width(32)) register_10 (.D(in_7), .en(and_10_out), .Q(register_10_q), .clk(clock_1_out), .clr(in_6));
  assign out_8 = decoder_2_out10 ? register_10_q : 32'bz;  // Controlled_Buffer controlled_buffer_10
  assign out_8 = decoder_2_out11 ? register_11_q : 32'bz;  // Controlled_Buffer controlled_buffer_11
  Register #(.width(32)) register_11 (.D(in_7), .en(and_11_out), .Q(register_11_q), .clk(clock_1_out), .clr(in_6));
  assign out_8 = decoder_2_out12 ? register_12_q : 32'bz;  // Controlled_Buffer controlled_buffer_12
  Register #(.width(32)) register_12 (.D(in_7), .en(and_12_out), .Q(register_12_q), .clk(clock_1_out), .clr(in_6));
  assign out_8 = decoder_2_out13 ? register_13_q : 32'bz;  // Controlled_Buffer controlled_buffer_13
  Register #(.width(32)) register_13 (.D(in_7), .en(and_13_out), .Q(register_13_q), .clk(clock_1_out), .clr(in_6));
  assign out_8 = decoder_2_out14 ? register_14_q : 32'bz;  // Controlled_Buffer controlled_buffer_14
  Register #(.width(32)) register_14 (.D(in_7), .en(and_14_out), .Q(register_14_q), .clk(clock_1_out), .clr(in_6));
  assign out_8 = decoder_2_out15 ? register_15_q : 32'bz;  // Controlled_Buffer controlled_buffer_15
  Register #(.width(32)) register_15 (.D(in_7), .en(and_15_out), .Q(register_15_q), .clk(clock_1_out), .clr(in_6));
  assign out_8 = decoder_2_out16 ? register_16_q : 32'bz;  // Controlled_Buffer controlled_buffer_16
  Register #(.width(32)) register_16 (.D(in_7), .en(and_16_out), .Q(register_16_q), .clk(clock_1_out), .clr(in_6));
  assign out_8 = decoder_2_out17 ? register_17_q : 32'bz;  // Controlled_Buffer controlled_buffer_17
  Register #(.width(32)) register_17 (.D(in_7), .en(and_17_out), .Q(register_17_q), .clk(clock_1_out), .clr(in_6));
  assign out_8 = decoder_2_out18 ? register_18_q : 32'bz;  // Controlled_Buffer controlled_buffer_18
  Register #(.width(32)) register_18 (.D(in_7), .en(and_18_out), .Q(register_18_q), .clk(clock_1_out), .clr(in_6));
  assign out_8 = decoder_2_out19 ? register_19_q : 32'bz;  // Controlled_Buffer controlled_buffer_19
  Register #(.width(32)) register_19 (.D(in_7), .en(and_19_out), .Q(register_19_q), .clk(clock_1_out), .clr(in_6));
  assign out_8 = decoder_2_out20 ? register_20_q : 32'bz;  // Controlled_Buffer controlled_buffer_20
  Register #(.width(32)) register_20 (.D(in_7), .en(and_20_out), .Q(register_20_q), .clk(clock_1_out), .clr(in_6));
  assign out_8 = decoder_2_out21 ? register_21_q : 32'bz;  // Controlled_Buffer controlled_buffer_21
  Register #(.width(32)) register_21 (.D(in_7), .en(and_21_out), .Q(register_21_q), .clk(clock_1_out), .clr(in_6));
  assign out_8 = decoder_2_out22 ? register_22_q : 32'bz;  // Controlled_Buffer controlled_buffer_22
  Register #(.width(32)) register_22 (.D(in_7), .en(and_22_out), .Q(register_22_q), .clk(clock_1_out), .clr(in_6));
  assign out_8 = decoder_2_out23 ? register_23_q : 32'bz;  // Controlled_Buffer controlled_buffer_23
  Register #(.width(32)) register_23 (.D(in_7), .en(and_23_out), .Q(register_23_q), .clk(clock_1_out), .clr(in_6));
  assign out_8 = decoder_2_out24 ? register_24_q : 32'bz;  // Controlled_Buffer controlled_buffer_24
  Register #(.width(32)) register_24 (.D(in_7), .en(and_24_out), .Q(register_24_q), .clk(clock_1_out), .clr(in_6));
  assign out_8 = decoder_2_out25 ? register_25_q : 32'bz;  // Controlled_Buffer controlled_buffer_25
  Register #(.width(32)) register_25 (.D(in_7), .en(and_25_out), .Q(register_25_q), .clk(clock_1_out), .clr(in_6));
  assign out_8 = decoder_2_out26 ? register_26_q : 32'bz;  // Controlled_Buffer controlled_buffer_26
  Register #(.width(32)) register_26 (.D(in_7), .en(and_26_out), .Q(register_26_q), .clk(clock_1_out), .clr(in_6));
  assign out_8 = decoder_2_out27 ? register_27_q : 32'bz;  // Controlled_Buffer controlled_buffer_27
  Register #(.width(32)) register_27 (.D(in_7), .en(and_27_out), .Q(register_27_q), .clk(clock_1_out), .clr(in_6));
  assign out_8 = decoder_2_out28 ? register_28_q : 32'bz;  // Controlled_Buffer controlled_buffer_28
  Register #(.width(32)) register_28 (.D(in_7), .en(and_28_out), .Q(register_28_q), .clk(clock_1_out), .clr(in_6));
  assign out_8 = decoder_2_out29 ? register_29_q : 32'bz;  // Controlled_Buffer controlled_buffer_29
  Register #(.width(32)) register_29 (.D(in_7), .en(and_29_out), .Q(register_29_q), .clk(clock_1_out), .clr(in_6));
  assign out_8 = decoder_2_out30 ? register_30_q : 32'bz;  // Controlled_Buffer controlled_buffer_30
  Register #(.width(32)) register_30 (.D(in_7), .en(and_30_out), .Q(register_30_q), .clk(clock_1_out), .clr(in_6));
  assign out_8 = decoder_2_out31 ? register_31_q : 32'bz;  // Controlled_Buffer controlled_buffer_31
  Register #(.width(32)) register_31 (.D(in_7), .en(and_31_out), .Q(register_31_q), .clk(clock_1_out), .clr(in_6));
  Decoder #(.select(5)) decoder_2 (
    .out0(decoder_2_out0), .out1(decoder_2_out1), .out2(decoder_2_out2), .out3(decoder_2_out3),
    .out4(decoder_2_out4), .out5(decoder_2_out5), .out6(decoder_2_out6), .out7(decoder_2_out7),
    .out8(decoder_2_out8), .out9(decoder_2_out9), .out10(decoder_2_out10), .out11(decoder_2_out11),
    .out12(decoder_2_out12), .out13(decoder_2_out13), .out14(decoder_2_out14), .out15(decoder_2_out15),
    .out16(decoder_2_out16), .out17(decoder_2_out17), .out18(decoder_2_out18), .out19(decoder_2_out19),
    .out20(decoder_2_out20), .out21(decoder_2_out21), .out22(decoder_2_out22), .out23(decoder_2_out23),
    .out24(decoder_2_out24), .out25(decoder_2_out25), .out26(decoder_2_out26), .out27(decoder_2_out27),
    .out28(decoder_2_out28), .out29(decoder_2_out29), .out30(decoder_2_out30), .out31(decoder_2_out31),
    .sel(in_1), .en(in_4));
  assign out_8 = decoder_2_out0 ? {32{1'b0}} : 32'bz;  // Controlled_Buffer controlled_buffer_32
  Decoder #(.select(5)) decoder_3 (
    .out0(decoder_3_out0), .out1(decoder_3_out1), .out2(decoder_3_out2), .out3(decoder_3_out3),
    .out4(decoder_3_out4), .out5(decoder_3_out5), .out6(decoder_3_out6), .out7(decoder_3_out7),
    .out8(decoder_3_out8), .out9(decoder_3_out9), .out10(decoder_3_out10), .out11(decoder_3_out11),
    .out12(decoder_3_out12), .out13(decoder_3_out13), .out14(decoder_3_out14), .out15(decoder_3_out15),
    .out16(decoder_3_out16), .out17(decoder_3_out17), .out18(decoder_3_out18), .out19(decoder_3_out19),
    .out20(decoder_3_out20), .out21(decoder_3_out21), .out22(decoder_3_out22), .out23(decoder_3_out23),
    .out24(decoder_3_out24), .out25(decoder_3_out25), .out26(decoder_3_out26), .out27(decoder_3_out27),
    .out28(decoder_3_out28), .out29(decoder_3_out29), .out30(decoder_3_out30), .out31(decoder_3_out31),
    .sel(in_2), .en(in_4));
  assign out_9 = decoder_3_out1 ? register_1_q : 32'bz;  // Controlled_Buffer controlled_buffer_33
  assign out_9 = decoder_3_out2 ? register_2_q : 32'bz;  // Controlled_Buffer controlled_buffer_34
  assign out_9 = decoder_3_out3 ? register_3_q : 32'bz;  // Controlled_Buffer controlled_buffer_35
  assign out_9 = decoder_3_out4 ? register_4_q : 32'bz;  // Controlled_Buffer controlled_buffer_36
  assign out_9 = decoder_3_out5 ? register_5_q : 32'bz;  // Controlled_Buffer controlled_buffer_37
  assign out_9 = decoder_3_out6 ? register_6_q : 32'bz;  // Controlled_Buffer controlled_buffer_38
  assign out_9 = decoder_3_out7 ? register_7_q : 32'bz;  // Controlled_Buffer controlled_buffer_39
  assign out_9 = decoder_3_out8 ? register_8_q : 32'bz;  // Controlled_Buffer controlled_buffer_40
  assign out_9 = decoder_3_out9 ? register_9_q : 32'bz;  // Controlled_Buffer controlled_buffer_41
  assign out_9 = decoder_3_out10 ? register_10_q : 32'bz;  // Controlled_Buffer controlled_buffer_42
  assign out_9 = decoder_3_out11 ? register_11_q : 32'bz;  // Controlled_Buffer controlled_buffer_43
  assign out_9 = decoder_3_out12 ? register_12_q : 32'bz;  // Controlled_Buffer controlled_buffer_44
  assign out_9 = decoder_3_out13 ? register_13_q : 32'bz;  // Controlled_Buffer controlled_buffer_45
  assign out_9 = decoder_3_out14 ? register_14_q : 32'bz;  // Controlled_Buffer controlled_buffer_46
  assign out_9 = decoder_3_out15 ? register_15_q : 32'bz;  // Controlled_Buffer controlled_buffer_47
  assign out_9 = decoder_3_out16 ? register_16_q : 32'bz;  // Controlled_Buffer controlled_buffer_48
  assign out_9 = decoder_3_out17 ? register_17_q : 32'bz;  // Controlled_Buffer controlled_buffer_49
  assign out_9 = decoder_3_out18 ? register_18_q : 32'bz;  // Controlled_Buffer controlled_buffer_50
  assign out_9 = decoder_3_out19 ? register_19_q : 32'bz;  // Controlled_Buffer controlled_buffer_51
  assign out_9 = decoder_3_out20 ? register_20_q : 32'bz;  // Controlled_Buffer controlled_buffer_52
  assign out_9 = decoder_3_out21 ? register_21_q : 32'bz;  // Controlled_Buffer controlled_buffer_53
  assign out_9 = decoder_3_out22 ? register_22_q : 32'bz;  // Controlled_Buffer controlled_buffer_54
  assign controlled_buffer_55_out = decoder_3_out23 ? register_23_q : 32'bz;  // Controlled_Buffer controlled_buffer_55
  assign out_9 = decoder_3_out24 ? register_24_q : 32'bz;  // Controlled_Buffer controlled_buffer_56
  assign out_9 = decoder_3_out25 ? register_25_q : 32'bz;  // Controlled_Buffer controlled_buffer_57
  assign out_9 = decoder_3_out26 ? register_26_q : 32'bz;  // Controlled_Buffer controlled_buffer_58
  assign out_9 = decoder_3_out27 ? register_27_q : 32'bz;  // Controlled_Buffer controlled_buffer_59
  assign out_9 = decoder_3_out28 ? register_28_q : 32'bz;  // Controlled_Buffer controlled_buffer_60
  assign out_9 = decoder_3_out29 ? register_29_q : 32'bz;  // Controlled_Buffer controlled_buffer_61
  assign out_9 = decoder_3_out30 ? register_30_q : 32'bz;  // Controlled_Buffer controlled_buffer_62
  assign out_9 = decoder_3_out31 ? register_31_q : 32'bz;  // Controlled_Buffer controlled_buffer_63
  assign out_9 = decoder_3_out0 ? {32{1'b0}} : 32'bz;  // Controlled_Buffer controlled_buffer_64

  // Notes on the sheet:
  //   MOHAMMED NASSER ALMARHOON MA01
endmodule
